# Fritzing sketch superMaquina (saved by Fritzing 0.9.3b)
circuit board: 6.94388cm x 5.54826cm
breadboards: 1

parts:
  R2 = Resistor [tolerance=±5% resistance=330 package=THT]
  LED2 = LED - 5mm [color="Red (633nm)" package="5 mm [THT]"]
  LED3 = LED - 5mm [color="Red (633nm)" package="5 mm [THT]"]
  LED4 = LED - 5mm [color="Red (633nm)" package="5 mm [THT]"]
  R3 = Resistor [tolerance=±5% resistance=330 package=THT]
  Componente1 = Arduino Uno (Rev3)
  R1 = Resistor [tolerance=±5% resistance=330 package=THT]

nets:
  N1: R2.Pin_0, LED2.cathode
  N2: R2.Pin_1, R3.Pin_0, Componente1.GND, R1.Pin_0
  N3: LED2.anode, Componente1.D12/MISO
  N4: LED3.cathode, R1.Pin_1
  N5: LED3.anode, Componente1.D13/SCK
  N6: LED4.cathode, R3.Pin_1
  N7: LED4.anode, Componente1.D11_PWM/MOSI

// code stored in the sketch: superMaquina.ino
/**
 * Sequencial de LEDs  (efeito Supermáquina)
 * @Author Eugenio Ramos Junior 
 */
 

 void setup() {
  pinMode(13, OUTPUT);
}

void loop() {
  digitalWrite(13, HIGH); 
}
